// Logisim project PROJET - DYMKO - MANUEL.circ as structural Verilog: 6 circuits, main circuit unité de calcul PARTIE 1
module \unité_de_calcul_PARTIE_1  (
  input  [7:0] in_1,
  input  [7:0] in_2,
  input  [7:0] in_3,
  output [7:0] out_4,
  output out_5
);

  wire adder_1_cout, soustracteur_en_valeur_absolut_1_out_4;
  wire [7:0] adder_1_out, divider_1_out, divider_1_rem, multiplier_1_cout, multiplier_1_out,
       soustracteur_en_valeur_absolut_1_out_3;

  Adder adder_1 (.a(in_1), .b(in_2), .out(adder_1_out), .cout(adder_1_cout));  // open: cin
  Soustracteur_en_valeur_absolut soustracteur_en_valeur_absolut_1 (
    .in_1(in_1), .in_2(in_2), .out_3(soustracteur_en_valeur_absolut_1_out_3),
    .out_4(soustracteur_en_valeur_absolut_1_out_4));
  \Séquenseur_interne  \séquenseur_interne_1  (
    .in_9(in_3[0]), .in_10(in_3[1]), .in_11(in_3[2]), .in_1(adder_1_cout),
    .in_2(soustracteur_en_valeur_absolut_1_out_4), .in_3(multiplier_1_cout), .in_4(divider_1_rem),
    .in_5(adder_1_out), .in_6(soustracteur_en_valeur_absolut_1_out_3), .in_7(multiplier_1_out),
    .in_8(divider_1_out), .out_12(out_4), .out_13(out_5));
  Multiplier multiplier_1 (.a(in_1), .b(in_2), .out(multiplier_1_out), .cout(multiplier_1_cout));  // open: cin
  Divider divider_1 (.a(in_1), .b(in_2), .out(divider_1_out), .rem(divider_1_rem));  // open: upper
endmodule

module \Séquenseur_interne  (
  input  in_1,
  input  in_2,
  input  [7:0] in_3,
  input  [7:0] in_4,
  input  [7:0] in_5,
  input  [7:0] in_6,
  input  [7:0] in_7,
  input  [7:0] in_8,
  input  in_9,
  input  in_10,
  input  in_11,
  output [7:0] out_12,
  output out_13
);

  wire and_1_out, and_2_out, and_3_out, and_4_out, and_5_out, and_6_out, and_7_out, and_8_out, and_9_out,
       nor_1_p3, nor_1_p4, nor_2_out, nor_3_out, not_1_out, or_1_out, or_2_out, undriven, undriven_2;
  wire [7:0] \valideur_d_octét_1_out_3 , \valideur_d_octét_2_out_3 , \valideur_d_octét_3_out_3 ,
       \valideur_d_octét_4_out_3 ;

  and and_1 (and_1_out, in_9, in_10, undriven);
  // NOR_Gate nor_1: pin names not known; wires that end beside it: in_10, in_11, nor_1_p3, nor_1_p4, in_9
  nor nor_2 (nor_2_out, nor_1_p3, in_9, in_11);
  or or_1 (or_1_out, in_3[7], in_3[6], in_3[5], in_3[4], in_3[3], in_3[2], in_3[1], in_3[0]);
  nor nor_3 (nor_3_out, in_10, undriven, in_10, in_10, nor_1_p4);
  not not_1 (not_1_out, in_11);
  and and_2 (and_2_out, in_9, nor_1_p4);
  and and_3 (and_3_out, in_10, nor_2_out, undriven_2);
  and and_4 (and_4_out, undriven_2, and_1_out, not_1_out);
  and and_5 (and_5_out, nor_3_out, in_11);
  and and_6 (and_6_out, in_1, and_2_out);
  or or_2 (or_2_out, in_4[7], in_4[6], in_4[5], in_4[4], in_4[3], in_4[2], in_4[1], in_4[0]);
  and and_7 (and_7_out, or_1_out, and_4_out);
  and and_8 (and_8_out, in_2, and_3_out);
  or or_3 (out_13, and_6_out, and_8_out, and_7_out, and_9_out);
  \Valideur_d_octét  \valideur_d_octét_1  (.in_2(and_3_out), .in_1(in_6), .out_3(\valideur_d_octét_1_out_3 ));
  \Valideur_d_octét  \valideur_d_octét_2  (.in_2(and_4_out), .in_1(in_7), .out_3(\valideur_d_octét_2_out_3 ));
  and and_9 (and_9_out, or_2_out, and_5_out);
  \Valideur_d_octét  \valideur_d_octét_3  (.in_2(and_2_out), .in_1(in_5), .out_3(\valideur_d_octét_3_out_3 ));
  \Valideur_d_octét  \valideur_d_octét_4  (.in_2(and_5_out), .in_1(in_8), .out_3(\valideur_d_octét_4_out_3 ));
  assign out_12 = \valideur_d_octét_3_out_3  | \valideur_d_octét_1_out_3  | \valideur_d_octét_2_out_3  | \valideur_d_octét_4_out_3 ;  // OR_Gate or_4, 8 bits wide
endmodule

module \Valideur_d_octét  (
  input  [7:0] in_1,
  input  in_2,
  output [7:0] out_3
);

  wire undriven, undriven_2, undriven_3, undriven_4, undriven_5, undriven_6, undriven_7;

  and and_1 (out_3[7], in_2, in_1[7], undriven);
  and and_2 (out_3[6], undriven, in_2, in_1[6], undriven_2);
  and and_3 (out_3[5], undriven_2, in_2, in_1[5], undriven_3);
  and and_4 (out_3[4], undriven_3, in_2, in_1[4], undriven_4);
  and and_5 (out_3[3], undriven_4, in_2, in_1[3], undriven_5);
  and and_6 (out_3[1], undriven_6, in_2, in_1[1], undriven_7);
  and and_7 (out_3[2], undriven_5, in_2, in_1[2], undriven_6);
  and and_8 (out_3[0], undriven_7, in_2, in_1[0]);
endmodule

// Soustracteur
module Soustracteur_en_valeur_absolut (
  input  [7:0] in_1,
  input  [7:0] in_2,
  output [7:0] out_3,
  output out_4
);

  wire [7:0] subtractor_1_out, subtractor_2_out;

  Comparator comparator_1 (.a(in_1), .b(in_2), .lt(out_4));  // open: gt, eq
  Subtractor subtractor_1 (.a(in_2), .b(in_1), .out(subtractor_1_out));  // open: bin, bout
  Subtractor subtractor_2 (.a(in_1), .b(in_2), .out(subtractor_2_out));  // open: bin, bout
  Multiplexer #(.width(8)) multiplexer_1 (
    .in0(subtractor_2_out), .in1(subtractor_1_out), .out(out_3), .sel(out_4));  // open: en
endmodule

module \unité_de_calcul_PARTIE_2  (
);

  wire _0_t, _3, clk, clr, comparator_1_eq, comparator_1_gt, comparator_3_eq, d_ff_1_q, d_ff_2_q, d_ff_3_q,
       d_ff_4_q, d_ff_5_q, d_ff_6_q, d_ff_7_q, d_ff_8_q, d_ff_9_q, imp, not_1_out, not_2_out, not_3_out,
       not_4_out, not_5_out, not_6_out, not_7_out, not_8_out, or_2_out, \unité_de_calcul_partie_1_1_out_5 ,
       X, Y;
  wire [7:0] controlled_buffer_1_out, controlled_buffer_2_out, controlled_buffer_3_out, counter_1_q,
       divider_1_rem, multiplexer_1_out, register_1_q, register_2_q, register_3_q, res, rom_1_data;

  Clock clock_1 (.out(clk));
  or or_1 (_3, comparator_1_eq, comparator_1_gt);
  Counter counter_1 (.Q(counter_1_q), .clk(clk), .clr(clr));  // open: load, D, count, carry
  D_Flip_Flop d_ff_1 (.Q(d_ff_1_q), .preset(res[7]), .reset(not_1_out));  // open: clk, D, Qn, en
  not not_1 (not_1_out, res[7]);
  Comparator comparator_1 (.a(counter_1_q), .b(8'h3), .gt(comparator_1_gt), .eq(comparator_1_eq));  // open: lt
  D_Flip_Flop d_ff_2 (.Q(d_ff_2_q), .preset(res[6]), .reset(not_2_out));  // open: clk, D, Qn, en
  not not_2 (not_2_out, res[6]);
  Comparator comparator_2 (.a(counter_1_q), .b({8{1'b0}}), .gt(_0_t), .eq(X));  // open: lt
  LED led_1 (.in(d_ff_2_q));
  LED led_2 (.in(d_ff_3_q));
  LED led_3 (.in(d_ff_4_q));
  LED led_4 (.in(d_ff_1_q));
  D_Flip_Flop d_ff_3 (.Q(d_ff_3_q), .preset(res[5]), .reset(not_3_out));  // open: clk, D, Qn, en
  not not_3 (not_3_out, res[5]);
  Divider divider_1 (.a(counter_1_q), .b(8'h2), .rem(divider_1_rem));  // open: out, upper
  LED led_5 (.in(d_ff_5_q));
  LED led_6 (.in(d_ff_7_q));
  LED led_7 (.in(d_ff_6_q));
  LED led_8 (.in(d_ff_8_q));
  Comparator comparator_3 (.a(divider_1_rem), .b({8{1'b0}}), .gt(imp), .eq(comparator_3_eq));  // open: lt
  or or_2 (or_2_out, X, _3);
  ROM rom_1 (.addr(counter_1_q), .data(rom_1_data));  // open: sel
  assign controlled_buffer_1_out = or_2_out ? rom_1_data : 8'bz;  // Controlled_Buffer controlled_buffer_1
  LED led_9 (.in(d_ff_9_q));
  D_Flip_Flop d_ff_4 (.Q(d_ff_4_q), .preset(res[4]), .reset(not_4_out));  // open: clk, D, Qn, en
  not not_4 (not_4_out, res[4]);
  Multiplexer #(.width(8)) multiplexer_1 (
    .in0(controlled_buffer_1_out), .in1(res), .out(multiplexer_1_out), .sel(_3));  // open: en
  D_Flip_Flop d_ff_5 (.Q(d_ff_5_q), .preset(res[3]), .reset(not_5_out));  // open: clk, D, Qn, en
  not not_5 (not_5_out, res[3]);
  and and_1 (Y, _0_t, comparator_3_eq);
  Register register_1 (.D(multiplexer_1_out), .Q(register_1_q), .clk(clk), .clr(clr));  // open: en
  assign controlled_buffer_2_out = imp ? rom_1_data : 8'bz;  // Controlled_Buffer controlled_buffer_2
  Register register_2 (.D(controlled_buffer_2_out), .Q(register_2_q), .clk(clk), .clr(clr));  // open: en
  assign controlled_buffer_3_out = Y ? rom_1_data : 8'bz;  // Controlled_Buffer controlled_buffer_3
  D_Flip_Flop d_ff_6 (.Q(d_ff_6_q), .preset(res[2]), .reset(not_6_out));  // open: clk, D, Qn, en
  not not_6 (not_6_out, res[2]);
  Register register_3 (.D(controlled_buffer_3_out), .Q(register_3_q), .clk(clk), .clr(clr));  // open: en
  D_Flip_Flop d_ff_7 (.Q(d_ff_7_q), .preset(res[1]), .reset(not_7_out));  // open: clk, D, Qn, en
  not not_7 (not_7_out, res[1]);
  Button button_1 (.out(clr));
  \unité_de_calcul_PARTIE_1  \unité_de_calcul_partie_1_1  (
    .in_1(register_1_q), .in_2(register_3_q), .in_3(register_2_q), .out_4(res),
    .out_5(\unité_de_calcul_partie_1_1_out_5 ));
  D_Flip_Flop d_ff_8 (.Q(d_ff_8_q), .preset(res[0]), .reset(not_8_out));  // open: clk, D, Qn, en
  not not_8 (not_8_out, res[0]);
  D_Flip_Flop d_ff_9 (.Q(d_ff_9_q), .preset(\unité_de_calcul_partie_1_1_out_5 ), .reset(clr));  // open: clk, D, Qn, en
endmodule

module Sequenseur_global (
  input  in_1,
  input  in_2,
  output out_3,
  output [7:0] out_4,
  output out_5,
  output out_6,
  output out_7,
  output out_8
);

  wire and_1_out, d_ff_1_qn;

  Counter counter_1 (.Q(out_4), .clk(in_1));  // open: load, D, count, carry, clr
  and and_1 (and_1_out, 1'b1, in_2);
  D_Flip_Flop d_ff_1 (.Q(out_5), .Qn(d_ff_1_qn), .preset(and_1_out));  // open: clk, D, en, reset
endmodule
